# Fritzing sketch Embedded device (saved by Fritzing 1.0.1rc)
breadboards: 1

parts:
  PIR1 = PIR sensor
  Part1 = Arduino Uno (Rev3) - ICSP
  DFRobot_DFPlayer_Mini1 = DFRobot DFPlayer Mini [part_number=DFR0299]
  LED1 = smd LED [color="Red (633nm)" package="1206 [SMD]"]
  SP1 = SPEAKER [package=pcb_mount_speaker]
  SP2 = SPEAKER [package=pcb_mount_speaker]
  LED2 = smd LED [color="Red (633nm)" package="1206 [SMD]"]
  R1 = Resistor [tolerance=±5% resistance=220 package="2512 [SMD]"]
  R2 = Resistor [tolerance=±5% resistance=220 package="2512 [SMD]"]
  R3 = Resistor [tolerance=±5% resistance=1k package="2512 [SMD]"]
  SERVO1 = Tower Pro SG90 servo [part_number=101246]  # not connected
  Grove1 = Grove OLED 128x96

nets:
  VDD: PIR1.VDD, Part1.3V3
  N1: PIR1.SIG, Part1.D2
  GND: PIR1.GND, Part1.GND, DFRobot_DFPlayer_Mini1.GND-1, DFRobot_DFPlayer_Mini1.GND-2, R1.Pin_0, R2.Pin_0, Grove1.GND
  N2: Part1.A4/SDA, Grove1.SDA
  N3: Part1.A5/SCL, Grove1.SCL
  N4: Part1.D10_PWM/SS, DFRobot_DFPlayer_Mini1.TX
  N5: Part1.D11_PWM/MOSI, DFRobot_DFPlayer_Mini1.RX, R3.Pin_0, R3.Pin_1
  N6: Part1.D6_PWM, LED2.cathode
  N7: Part1.D7, LED1.cathode
  VCC: Part1.5V, DFRobot_DFPlayer_Mini1.VCC, Grove1.VCC
  N8: DFRobot_DFPlayer_Mini1.SPK_1, SP1.-, SP2.-
  N9: DFRobot_DFPlayer_Mini1.SPK_2, SP1.+, SP2.+
  N10: LED1.anode, R1.Pin_1
  N11: LED2.anode, R2.Pin_1

custom parts:
  Tower Pro SG90 servo: Original file by John De Cristofaro http://www.adafruit.com/products/1449 Adafruit Feedback Servo (Small) Edited by: e-radionica.com 28/9/2015
