# Fritzing sketch circuit_Arduino_DFPlayer_ESP8266_PIR_sensor (saved by Fritzing 1.0.1rc)
breadboards: 1

parts:
  PIR1 = PIR sensor
  Part1 = Arduino Uno (Rev3) - ICSP
  DFRobot_DFPlayer_Mini1 = DFRobot DFPlayer Mini [part_number=DFR0299]
  LED1 = smd LED [color="Red (633nm)" package="1206 [SMD]"]
  SP1 = SPEAKER [package=pcb_mount_speaker]
  SP2 = SPEAKER [package=pcb_mount_speaker]
  LED2 = smd LED [color="Red (633nm)" package="1206 [SMD]"]
  R1 = Resistor [tolerance=±5% resistance=220 package="2512 [SMD]"]
  R2 = Resistor [tolerance=±5% resistance=220 package="2512 [SMD]"]
  R3 = Resistor [tolerance=±5% resistance=1k package="2512 [SMD]"]
  WeMos_D1_Mini2 = WeMos D1 Mini
  R4 = Resistor [tolerance=±5% resistance=1k package="2512 [SMD]"]

nets:
  VDD: PIR1.VDD, Part1.D9_PWM, Part1.5V, DFRobot_DFPlayer_Mini1.VCC
  N1: PIR1.SIG, Part1.D2
  GND: PIR1.GND, Part1.D11_PWM/MOSI, Part1.GND, DFRobot_DFPlayer_Mini1.GND-1, DFRobot_DFPlayer_Mini1.GND-2, LED1.cathode, LED2.cathode, WeMos_D1_Mini2.G, R4.Pin_0
  N2: Part1.D8, WeMos_D1_Mini2.TX
  N3: Part1.D10_PWM/SS, DFRobot_DFPlayer_Mini1.TX
  N4: Part1.D6_PWM, R1.Pin_0
  N5: Part1.D7, R2.Pin_0
  N6: DFRobot_DFPlayer_Mini1.RX, R3.Pin_0, R3.Pin_1
  N7: DFRobot_DFPlayer_Mini1.SPK_1, SP1.-, SP2.-
  N8: DFRobot_DFPlayer_Mini1.SPK_2, SP1.+, SP2.+
  N9: LED1.anode, R1.Pin_1
  N10: LED2.anode, R2.Pin_1
